# Fritzing sketch DAC 1.1.1 (saved by Fritzing 0.9.3b)
circuit board: 3.62cm x 11.1345cm
breadboards: 1

parts:
  Q3 = TRANSISTOR_NPN [package=to-92]
  R5 = Resistor [tolerance=±5% resistance=100k package=THT]
  R6 = Resistor [tolerance=±5% resistance=33k package=THT]
  Q4 = TRANSISTOR_NPN [package=to-92]
  R7 = Resistor [tolerance=±5% resistance=100k package=THT]
  R8 = Resistor [tolerance=±5% resistance=33k package=THT]
  Q1 = TRANSISTOR_NPN [package=to-92]
  R1 = Resistor [tolerance=±5% resistance=100k package=THT]
  Q2 = TRANSISTOR_NPN [package=to-92]
  R3 = Resistor [tolerance=±5% resistance=100k package=THT]
  R4 = Resistor [tolerance=±5% resistance=33k package=THT]
  R25 = Resistor [tolerance=±5% resistance=100 package=THT]
  R26 = Resistor [tolerance=±5% resistance=100 package=THT]
  R27 = Resistor [tolerance=±5% resistance=100 package=THT]
  R28 = Resistor [tolerance=±5% resistance=100 package=THT]
  DAC1 = IC, DIP package, 14 pins [chip_label="DAC MCP4922"]
  DAC2 = IC, DIP package, 14 pins [chip_label="DAC MCP4922"]
  R2 = Resistor [tolerance=±5% resistance=33k package=THT]
  Power_and_I2C_Header = double row male pin header, 8 pins [form="♂ (male)"]
  Teensy_3_2 = Teensy 3.2 [part_number="Teensy 3.2"]
  Expander_Header = double row male pin header, 14 pins [form="♂ (male)"]
  CV_Output_Buffer = MCP6004 [part_number=MCP6004 package="DIP (Dual Inline) [THT]"]
  J5 = female pin header, 3 pins [form="♀ (female)"]  # not connected
  Eurorack_Power_Header = double row male pin header, 10 pins [form="♂ (male)"]
  +7-12V = female pin header, 2 pins [form="♀ (female)"]
  Reg_5V = male pin header, 2 pins [form="♂ (male)"]
  NC = female pin header, 1 pin [form="♀ (female)"]  # not connected
  Interface_Pots = female pin header, 5 pins [form="♀ (female)"]
  J2 = male pin header, 5 pins [form="♂ (male)"]
  CV_in = female pin header, 5 pins [form="♀ (female)"]
  CV_Out = male pin header, 4 pins [form="♂ (male)"]
  78L05 = Voltage Regulator [package=to-92]
  C1 = Ceramic Capacitor [capacitance=0.33µF package="100 mil [THT, multilayer]"]
  C2 = Ceramic Capacitor [capacitance=100nF package="100 mil [THT, multilayer]"]
  R29 = Resistor [tolerance=±5% resistance=100 package=THT]
  R30 = Resistor [tolerance=±5% resistance=100 package=THT]
  R31 = Resistor [tolerance=±5% resistance=100 package=THT]
  R32 = Resistor [tolerance=±5% resistance=100 package=THT]
  j4 = female pin header, 14 pins [form="♀ (female)"]  # not connected
  J3 = female pin header, 14 pins [form="♀ (female)"]
  J7 = female pin header, 7 pins [form="♀ (female)"]
  J8 = female pin header, 7 pins [form="♀ (female)"]  # not connected
  J6 = female pin header, 5 pins [form="♀ (female)"]
  J9 = female pin header, 1 pin [form="♀ (female)"]  # not connected

nets:
  GND: Q3.E, R6.Pin_1, Q4.E, R8.Pin_1, Q1.E, Q2.E, R4.Pin_1, DAC1.pin8, DAC1.pin12, DAC2.pin8, DAC2.pin12, R2.Pin_1, Power_and_I2C_Header.pin1, Power_and_I2C_Header.pin8, Teensy_3_2.GND#16, Teensy_3_2.GND#49, Expander_Header.pin2, Expander_Header.pin13, CV_Output_Buffer.Vss(GND), Eurorack_Power_Header.pin2, Eurorack_Power_Header.pin3, Eurorack_Power_Header.pin4, Eurorack_Power_Header.pin7, Eurorack_Power_Header.pin8, Eurorack_Power_Header.pin9, +7-12V.pin2, J2.pin1, 78L05.IN, C1.1, C2.1
  N1: Q3.B, R5.Pin_1, R6.Pin_0
  TRIG 3: Q3.C, Teensy_3_2.D3
  N2: R5.Pin_0, J2.pin3
  N3: Q4.B, R7.Pin_1, R8.Pin_0
  TRIG 4: Q4.C, Teensy_3_2.D0
  N4: R7.Pin_0, J2.pin2
  N5: Q1.B, R1.Pin_1, R2.Pin_0
  TRIG 1: Q1.C, Teensy_3_2.D4
  N6: R1.Pin_0, J2.pin5
  N7: Q2.B, R3.Pin_1, R4.Pin_0
  TRIG 2: Q2.C, Teensy_3_2.D5
  N8: R3.Pin_0, J2.pin4
  N9: R25.Pin_0, CV_in.pin5
  N10: R25.Pin_1, Teensy_3_2.A2/D16
  N11: R26.Pin_0, CV_in.pin4
  N12: R26.Pin_1, Teensy_3_2.A3/D17
  N13: R27.Pin_0, CV_in.pin3
  N14: R27.Pin_1, Teensy_3_2.A6/D20
  N15: R28.Pin_0, CV_in.pin2
  N16: R28.Pin_1, Teensy_3_2.A7/D21
  5V: DAC1.pin1, DAC1.pin9, DAC1.pin11, DAC1.pin13, DAC2.pin1, DAC2.pin9, DAC2.pin11, DAC2.pin13, Power_and_I2C_Header.pin2, Power_and_I2C_Header.pin7, Teensy_3_2.Vin, Expander_Header.pin1, CV_Output_Buffer.Vdd(+), Reg_5V.pin1, J3.pin14
  N17: DAC1.pin3, Teensy_3_2.D1
  SCK: DAC1.pin4, DAC2.pin4, Teensy_3_2.A0/D14, J3.pin2
  MOSI: DAC1.pin5, DAC2.pin5, Teensy_3_2.D7
  CV OUT B: DAC1.pin10, CV_Output_Buffer.+IN_2
  CV OUT A: DAC1.pin14, CV_Output_Buffer.+IN_1
  N18: DAC2.pin3, Teensy_3_2.D2
  CV OUT D: DAC2.pin10, CV_Output_Buffer.+IN_4
  CV OUT C: DAC2.pin14, CV_Output_Buffer.+IN_3
  3.3V: Power_and_I2C_Header.pin3, Power_and_I2C_Header.pin6, Teensy_3_2.3V3, Expander_Header.pin14, Interface_Pots.pin1
  N19: Power_and_I2C_Header.pin4, Teensy_3_2.D30, J7.pin2
  N20: Power_and_I2C_Header.pin5, Teensy_3_2.D29, J7.pin1
  N21: Teensy_3_2.D8, Expander_Header.pin12, CV_in.pin1
  N22: Teensy_3_2.D24, Expander_Header.pin5
  N23: Teensy_3_2.D25, Expander_Header.pin9
  N24: Teensy_3_2.D26, Expander_Header.pin6
  N25: Teensy_3_2.D27, Expander_Header.pin8
  N26: Teensy_3_2.D28, Expander_Header.pin7
  N27: Teensy_3_2.D31, Expander_Header.pin10
  N28: Teensy_3_2.A12, Interface_Pots.pin5
  N29: Teensy_3_2.A13, Interface_Pots.pin4
  N30: Teensy_3_2.A11, Interface_Pots.pin3
  N31: Teensy_3_2.A10, Interface_Pots.pin2
  N32: Expander_Header.pin3, J6.pin5
  N33: Expander_Header.pin4, J7.pin4
  N34: Expander_Header.pin11, J7.pin5
  N35: CV_Output_Buffer.Out_1, CV_Output_Buffer.-IN_1, R30.Pin_0
  N36: CV_Output_Buffer.-IN_2, CV_Output_Buffer.Out_2, R32.Pin_0
  N37: CV_Output_Buffer.Out_3, CV_Output_Buffer.-IN_3, R31.Pin_0
  N38: CV_Output_Buffer.-IN_4, CV_Output_Buffer.Out_4, R29.Pin_1
  N39: Eurorack_Power_Header.pin1, Eurorack_Power_Header.pin10, +7-12V.pin1, 78L05.OUT, C1.0
  N40: Eurorack_Power_Header.pin5, Eurorack_Power_Header.pin6
  N41: Reg_5V.pin2, 78L05.GND, C2.0
  N42: CV_Out.pin1, R32.Pin_1
  N43: CV_Out.pin2, R31.Pin_1
  N44: CV_Out.pin3, R30.Pin_1
  N45: CV_Out.pin4, R29.Pin_0

notes:
  Betweener, 1.1.1
  !!!!NOT POWER!!!!
  -12_Red Stripe
  GND
  DAC 1.1.0
  CC-BY-SA

custom parts:
  Teensy 3.2: Updated from Fabian Althaus. The Teensy is a complete USB-based microcontoller development system, in a very small footprint, capable of implementing many types of projects. All programming is done via the USB port. No special programmer is needed, only a standard micro-USB cable and a PC or Macintosh with a USB port.
  MCP6004: Quad Op-Amp with rail-to-rail output and low voltage operation
